# Fritzing sketch circuit (saved by Fritzing 0.9.3b)
breadboards: 1

parts:
  Part1 = Arduino Uno (Rev3)
  R1 = Resistor [tolerance=±5% resistance=10k package="0402 [SMD]"]
  S1 = SWITCH-MOMENTARY-2 [package=tactile-pth]
  S2 = SWITCH-MOMENTARY-2 [package=tactile-pth]
  S3 = SWITCH-MOMENTARY-2 [package=tactile-pth]
  S4 = SWITCH-MOMENTARY-2 [package=tactile-pth]
  S5 = SWITCH-MOMENTARY-2 [package=tactile-pth]
  R2 = Resistor [tolerance=±10% resistance=560 package=THT]
  R3 = Resistor [tolerance=±10% resistance=220 package=THT]
  R4 = Resistor [tolerance=±10% resistance=10k package=THT]
  R5 = Resistor [tolerance=±5% resistance=1M package=THT]
  LED1 = smd LED [color="Green (565nm)" package="1206 [SMD]"]
  R6 = Resistor [tolerance=±10% resistance=220 package=THT]
  LED2 = smd LED [color="Red (660nm)" package="1206 [SMD]"]
  R7 = Resistor [tolerance=±10% resistance=220 package=THT]

nets:
  N1: Part1.A0, R1.Pin_1, S1.1, S2.1, S3.1, S4.1, S5.1
  N2: Part1.D12/MISO, R7.Pin_0
  N3: Part1.D13/SCK, R6.Pin_0
  N4: Part1.GND, R1.Pin_0, LED1.cathode, LED2.cathode
  N5: Part1.5V, S5.2, R2.Pin_1, R3.Pin_1, R4.Pin_1, R5.Pin_1
  N6: S1.2, R5.Pin_0
  N7: S2.2, R4.Pin_0
  N8: S3.2, R3.Pin_0
  N9: S4.2, R2.Pin_0
  N10: LED1.anode, R6.Pin_1
  N11: LED2.anode, R7.Pin_1
